# Fritzing sketch diagram (saved by Fritzing 0.9.3b)
breadboards: 1

parts:
  Raspberry_Pi_1 = Raspberry Pi 3 [part_number=RPI-3-V1.2]
  DHT1 = DHT11 Humitidy and Temperature Sensor (3 pins)
  LED1 = LEDs [package=led10mm]
  SERVO1 = Tower Pro SG90 servo [part_number=101246]
  SERVO2 = Tower Pro SG90 servo [part_number=101246]
  R1 = Resistor [tolerance=±5% resistance=220 package=THT]
  CAMERA1 = TTL Serial JPEG Camera  # not connected

nets:
  N1: Raspberry_Pi_1.GPIO21, SERVO2.Signal
  N2: Raspberry_Pi_1.GPIO20, SERVO1.Signal
  N3: Raspberry_Pi_1.GPIO16, DHT1.DATA
  N4: Raspberry_Pi_1.GPIO12, LED1.A
  GND: Raspberry_Pi_1.GND, DHT1.GND, SERVO1.GND, SERVO2.GND, R1.Pin_0
  +5V: Raspberry_Pi_1.5V, DHT1.VDD, SERVO1.+5V, SERVO2.+5V
  N5: LED1.C, R1.Pin_1

notes:
  Pi Camera
  TowerPro 9g
  DHT11

custom parts:
  DHT11 Humitidy and Temperature Sensor (3 pins): DHT11 Humidity and Temperature Sensor (3 pins) from the design created by John De Cristofaro for Adafruit Industries.
  Tower Pro SG90 servo: Original file by John De Cristofaro http://www.adafruit.com/products/1449 Adafruit Feedback Servo (Small) Edited by: e-radionica.com 28/9/2015
  TTL Serial JPEG Camera: TTL Serial JPEG Camera with NTSC Out
